# Fritzing sketch Touchbutton (saved by Fritzing 0.9.3b)

parts:
  R1 = Resistor [tolerance=±5% resistance=2.0 package=THT]
  Part2 = Arduino Micro (Rev3)
  C1 = Ceramic Capacitor [capacitance=100nF package="100 mil [THT, multilayer]"]

nets:
  N1: R1.Pin_1, Part2.D2/SDA
  N2: Part2.GND, C1.1
