# Fritzing sketch Volante (saved by Fritzing 0.9.3b)
breadboards: 2

parts:
  Part1 = Arduino Micro (Rev3)
  S1 = Pushbutton [package="[THT]"]
  S2 = Pushbutton [package="[THT]"]
  S3 = Pushbutton [package="[THT]"]
  S4 = Pushbutton [package="[THT]"]
  S5 = Pushbutton [package="[THT]"]
  S6 = Pushbutton [package="[THT]"]
  S7 = Pushbutton [package="[THT]"]
  S8 = Pushbutton [package="[THT]"]
  S9 = Pushbutton [package="[THT]"]
  S10 = Pushbutton [package="[THT]"]
  S11 = Pushbutton [package="[THT]"]
  S12 = Pushbutton [package="[THT]"]
  S13 = Pushbutton [package="[THT]"]
  S14 = Pushbutton [package="[THT]"]
  LED1 = LED - 5mm [color="Red (633nm)" package="5 mm [THT]"]
  U1 = POT [package=pot_mammoth]
  U2 = POT [package=pot_mammoth]
  S15 = Pushbutton [package="[THT]"]
  U3 = POT [package=pot_mammoth]

nets:
  N1: Part1.D1/TX, S4.Pin_1, S4.Pin_2
  N2: Part1.D0/RX, S1.Pin_1, S1.Pin_2
  N3: Part1.D2/SDA, S2.Pin_1, S2.Pin_2
  N4: Part1.D3/SCL, S3.Pin_1, S3.Pin_2
  N5: Part1.D4_PWM/A6, S8.Pin_1, S8.Pin_2
  N6: Part1.D5_PWM, Part1.GND, S1.Pin_3, S1.Pin_4, S2.Pin_3, S2.Pin_4, S3.Pin_3, S3.Pin_4, S4.Pin_3, S4.Pin_4, S5.Pin_3, S5.Pin_4, S6.Pin_3, S6.Pin_4, S7.Pin_3, S7.Pin_4, S8.Pin_3, S8.Pin_4, S9.Pin_1, S9.Pin_2, S10.Pin_1, S10.Pin_2, S11.Pin_1, S11.Pin_2, S12.Pin_1, S12.Pin_2, S13.Pin_1, S13.Pin_2, S14.Pin_1, S14.Pin_2, LED1.cathode, U1.E, U2.S, S15.Pin_1, S15.Pin_2, U3.E
  N7: Part1.D6_PWM/A7, S6.Pin_1, S6.Pin_2
  N8: Part1.D7, S5.Pin_1, S5.Pin_2
  N9: Part1.D8_PWM/A8, S9.Pin_3, S9.Pin_4
  N10: Part1.D9_PWM/A9, S11.Pin_3, S11.Pin_4
  N11: Part1.D10_PWM/A10, S10.Pin_3, S10.Pin_4
  N12: Part1.D11_PWM, S12.Pin_3, S12.Pin_4
  N13: Part1.D12_PWM/A11, S13.Pin_3, S13.Pin_4
  N14: Part1.5V, U1.S, U2.E, U3.S
  N15: Part1.A4, S15.Pin_3, S15.Pin_4
  N16: Part1.A3, LED1.anode
  N17: Part1.A2, U3.A
  N18: Part1.A1, U1.A
  N19: Part1.A0, U2.A
  N20: Part1.D13_PWM, S14.Pin_3, S14.Pin_4
  N21: S7.Pin_1, S7.Pin_2

notes:
  // switch buttons
  int up = 0;
  int down = 1;
  int left = 2;
  int right = 3;
  int square = 4;
  int cross = 5;
  int circle = 6;
  int triangle = 7;
  int L1 = 8;
  int L2 = 9;
  int R1 = 10;
  int R2 = 11;
  int select = 12;
  int start = 13;
  // steering and gas-brake potentiometers
  int st = A0;
  int gas = A1;
  AUTOFIRE to enable: keep press this button and the desired pad button
  International License
  Volante The Gamepad
  by Andrea Mancini
  is licensed under a
  Creative Commons Attribution 4.0
